# Fritzing sketch EsquemaEmisor (saved by Fritzing 0.9.1b)
breadboards: 1

parts:
  Parte1 = Arduino Mega 2560 (Rev3)
  Parte2 = Arduino Ethernet Shield (Rev3)
  Tx1 = mystery part, 3 pins [chip_label=?]
  LED1 = LED - 5mm [color="Red (633nm)" package="5 mm [THT]"]
  R1 = Resistor [tolerance=±5% resistance=220 package=THT]

nets:
  N1: Parte1.D39, Tx1.pin1
  N2: Parte1.GND, Tx1.pin3, LED1.anode
  N3: Parte2.D2, R1.Pin_0
  N4: Parte2.5V, Tx1.pin2
  N5: LED1.cathode, R1.Pin_1

notes:
  Emisor RF
  (Desconozco como conectar Ethernet y Mega)

// code stored in the sketch: Alimentador_Cleo.ino
//#include <Time.h>

//------------------------------------------- LIBRERIAS ------------------------------------------------
//---- Librerias de Red -----

//#include <EthernetClient.h>
#include <SPI.h>
#include <Ethernet.h>
//#include <EthernetServer.h>

//----- Libreria RF (https://www.minitronica.com/arduino-radiofrecuencia-433mhz-virtualwire/)
#include <VirtualWire.h>



//---- Librerias Servo

//#include <Servo.h>

//--------------------------

//---- Librerias Tarjeta SD

//#include <SD.h>


//------------------------

//------------------------------------------------------------------------------------------------------------


//-----Definiciones Globales
#define PORT 9090
#define LED_COM 2 
#define RF_TX   39 //PIN por el que envia el RF
#define DELAYS 2000
byte mac[] = { 0xFA, 0xBA, 0xDA, 0xFA, 0xBA, 0xDA }; //Mac del adaptador Ethernet.
IPAddress ip(192, 168, 1, 235); //IP asignada al mismo
IPAddress gateway(192,168,1, 1);
IPAddress subnet(255, 255, 255, 0);
EthernetServer server(PORT);


//Servo myservo;
//#define NOMFILE "feedCleo.txt"

void setup() {

  Serial.begin(9600);
  while (!Serial) {; }
  initPins();
  initNet();
  initRF();//Antes de llamar a esta funcion hay que establecer todos los PINS.
  //myservo.attach(9);
  //Serial.begin(9600);
  //setTime(19,58,00,6,11,2014);
}

//Funcion para inicializar la informacion de la interfaz de Red.
void initNet() 
{
  Ethernet.begin(mac, ip);
  
  server.begin();
  Serial.println(Ethernet.localIP());
  Serial.println("\n");
}

void initPins(){
  pinMode(LED_COM, OUTPUT);
}

void initRF(){
  vw_set_ptt_inverted(true); // Required for DR3100
  vw_setup(2000);
  vw_set_tx_pin(RF_TX);
  //vw_rx_start();   
}

void loop() {

  //Serial.print(hora);
  //if (hora == 1)
  //  alimentarCleo();

  //delay(60*1000);

  //Esperamos a que venga algun cliente

  
  
  EthernetClient client = server.available();
  if (client) {
    Serial.println("new client");
    // an http request ends with a blank line
    boolean currentLineIsBlank = true;
    while (client.connected()) 
    {
      while (client.available()>0){
        char c = client.read();
        Serial.print(c);
      }
      construirRespuestaHTTP(client);
      delay(10);
      client.stop();
      blinkLed(1);
      char chArray[] = {'1', '2'};
      sendRFMessage(chArray);
      delay(DELAYS);
      blinkLed(0);
      //Mostrar Respuesta
      
      break;
      
    }

    Serial.println("Cliente Desconectado.");
    Ethernet.maintain();
    
  }
  
}

void construirRespuestaHTTP(EthernetClient client){
  client.println("HTTP/1.1 200 OK");
  client.println("Content-Type: text/html");
  client.println("Connection: close");  
  client.println();
  client.println("<!DOCTYPE HTML>");
  client.println("<html>");
  client.println("Hecho!");
  
  client.println("</html>");
}
void blinkLed(int estado){
  //Encedemos el Led para saber que hay comunicacion
  digitalWrite(LED_COM, (estado == 1 ? HIGH: LOW));
}

void sendRFMessage(char value[]){
  vw_send((uint8_t *)value, strlen(value)); //Envia el mensaje
  vw_wait_tx(); //Espera hasta que se envien los datos
  delay(200);
  //La siguiente implementacion no la soporta la libreria que tengo
  /*if (vw_tx_active()){
    Serial.write("Enviado!!");
  }
  else{
    Serial.write("NO SE HA ENVIADO!!!!");
  }
  */
  Serial.println("Alimentando a Cleo");
}

//Accede a la tarjeta y recupera cuando ha sido la ultima vez que se ha alimentado a Cleo.
//Es necesario consultarlo, porque podemos alimentar en cualquier momento. Si la diferencia de horas es mayor a 12, se deberia alimentar
/*String getHoraUltimoAlimento(){

  String ret = "";
  File fich = SD.open(NOMFILE);
  if (fich)
  {
    //Nos quedamos con el ultimo registro que tenga
    while (fich.available()){

    }

    fich.close();
  }
  else{
    Serial.println("Error abiendo el fichero");
  }


  return ret;

  }*/

/*void writeLogToSD(){

  }

  void writeLogToRemoteBD(){

  }*/
