# Fritzing sketch EsquemaReceptor (saved by Fritzing 0.9.1b)
breadboards: 1

parts:
  Rx1 = mystery part, 4 pins [chip_label=? part_number=XD-RF-5V]
  Parte1 = Arduino Uno (Rev3)
  LED1 = LED - 5mm [color="Red (633nm)" package="5 mm [THT]"]
  R1 = Resistor [tolerance=±5% resistance=220 package=THT]
  J1 = Basic Servo [part_number=SG90]

nets:
  GND: Rx1.pin1, Parte1.GND, LED1.anode, J1.gnd
  N1: Rx1.pin2, Parte1.D3_PWM
  5V: Rx1.pin4, Parte1.5V, J1.vcc
  N2: Parte1.D9_PWM, J1.pulse
  N3: Parte1.D4, R1.Pin_0
  N4: LED1.cathode, R1.Pin_1

// code stored in the sketch: Alimentador_CleoReceptor.ino
#include <ServoTimer2.h>  // the servo library


#include <VirtualWire.h>



#define RF_RX     3
#define PIN_SERVO 9
#define LED_PIN   4
#define DELAYS    2000
ServoTimer2 servo;

void setup() {
  // put your setup code here, to run once:
  Serial.begin(9600);
  initPins();
  initRF();
  initServo();
  Serial.println("Setup");
}

void initPins(){
  pinMode(LED_PIN, OUTPUT);
}

void initServo(){
  servo.attach(PIN_SERVO);  // attaches the servo on pin 9 to the servo object
}

void initRF(){
  //vw_set_ptt_inverted(true); // Required for DR3100
  vw_setup(2000);
  vw_set_rx_pin(RF_RX);
  vw_rx_start();
}

void loop() {
  uint8_t buf[VW_MAX_MESSAGE_LEN];
  uint8_t dataLength=VW_MAX_MESSAGE_LEN;

 
  if (vw_get_message(buf,&dataLength))
  {
    Serial.println("Algo ha llegado.");
    if(buf[0]=='1')
    {
      blinkLed(1);
      delay(DELAYS);
      blinkLed(0);
      moveServo();
      
    }
  }
  //moveServo();
  delay(1);
}
void blinkLed(int estado){
  //Encedemos el Led para saber que hay comunicacion
  digitalWrite(LED_PIN, (estado == 1 ? HIGH: LOW));
}

void moveServo()
{
  Serial.println("Moviendo...");   
  
  servo.write(750);           
  delay(1000);
  //servo.write(1500);              
  //delay(1000);
  //servo.write(2250);            
  delay(1000);
  servo.write(3000);             
}
